# Fritzing sketch Stoplicht fritzing V1.1 (saved by Fritzing 0.9.3b)
breadboards: 1

parts:
  LED1 = LED - 5mm [color="Red (633nm)" package="5 mm [THT]"]
  R1 = Resistor [tolerance=±5% resistance=220 package=THT]
  LED2 = LED - 5mm [color="Red (633nm)" package="5 mm [THT]"]
  LED3 = LED - 5mm [color="Red (633nm)" package="5 mm [THT]"]
  LED4 = LED - 5mm [color="Red (633nm)" package="5 mm [THT]"]
  R2 = Resistor [tolerance=±5% resistance=220 package=THT]
  R3 = Resistor [tolerance=±5% resistance=220 package=THT]
  R4 = Resistor [tolerance=±5% resistance=220 package=THT]
  Onderdeel1 = Arduino BT

nets:
  N1: LED1.cathode, R1.Pin_1
  N2: LED1.anode, Onderdeel1.TX/D1
  N3: R1.Pin_0, R2.Pin_0, R3.Pin_0, R4.Pin_0, Onderdeel1.GND
  N4: LED2.cathode, R2.Pin_1
  N5: LED2.anode, Onderdeel1.D2
  N6: LED3.cathode, R3.Pin_1
  N7: LED3.anode, Onderdeel1.PWM_D3
  N8: LED4.cathode, R4.Pin_1
  N9: LED4.anode, Onderdeel1.D4
